// Logisim project log_circuit.circ as structural Verilog: 1 circuit, main circuit main
module main (
  input  [5:0] in_1,
  input  [5:0] in_2,
  output [5:0] out_3
);

  wire [5:0] adder_1_out, adder_2_out;

  Adder #(.width(6)) adder_1 (.a(in_1), .b(in_2), .out(adder_1_out));  // open: cin, cout
  Adder #(.width(6)) adder_2 (.a(adder_1_out), .b(6'b000011), .out(adder_2_out));  // open: cin, cout
  Adder #(.width(6)) adder_3 (.a(adder_2_out), .b(adder_1_out), .out(out_3));  // open: cin, cout
endmodule
