// Logisim project logi.circ as structural Verilog: 1 circuit, main circuit main
module main (
);

  Adder adder_1 ();  // open: a, b, out, cin, cout
  Multiplexer multiplexer_1 ();  // open: in0, in1, out, sel, en
  Multiplexer multiplexer_2 ();  // open: in0, in1, out, sel, en
  Multiplexer multiplexer_3 ();  // open: in0, in1, out, sel, en
  Multiplexer multiplexer_4 ();  // open: in0, in1, out, sel, en
endmodule
